# Fritzing sketch washing machine (saved by Fritzing 0.9.3b)
breadboards: 1

parts:
  U1 = NodeMCU V3.0
  SW-1 = Vibration sensor module
  M1 = DC Motor
  S1 = H-Bridge with L298N
  S4 = Magnetic Door Switch [package=reed_switch_plastic]
  JACK1 = 2.1mm Barrel Jack with Terminal Block

nets:
  N1: U1.D0, S1.ENB
  N2: U1.D1, S1.IN4
  N3: U1.D2, S1.IN3
  N4: U1.D3, SW-1.Digital_output
  N5: U1.D4, S4.2
  3V3: U1.3V3, SW-1.vcc, S4.1
  GND: U1.GND, SW-1.Ground, S1.GND, JACK1.NEG
  N6: M1.pin_1, S1.M2-02
  N7: M1.pin_2, S1.M2-01
  N8: S1.12V, JACK1.POS

custom parts:
  NodeMCU V3.0: ESP8266 based NodeMCU
  Vibration sensor module: Single-roller type full induction trigger switch. When no vibration or tilt, the product is ON conduction state, and in the steady state, when a vibration or tilt, the switch will be rendered instantly disconnect the conductive resistance increases, generating a current pulse signal, thereby triggering circuit. The default state of the swith is close Digital output Supply voltage:3.3V-5V On-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
  H-Bridge with L298N: h-bridge
